# Fritzing sketch IoT Project with notes (saved by Fritzing 0.9.9b)
breadboards: 1

parts:
  LED2 = LED - 5mm [color="Red (633nm)" current=0.030 package="5 mm [THT]"]
  Part4 = FC-28 Soil Hygrometer Module - Probe
  R4 = Resistor [tolerance=±5% power=0.25 resistance=330 package=THT]
  MCU1 = Raspberry Pi Zero
  Part5 = FC-28 Soil Hygrometer Module
  Part6 = DHT22 module
  e-radionica_com1 = LM393 LDR breakout [part_number=100027]

nets:
  GND: LED2.cathode, MCU1.pin_6, MCU1.pin_9, MCU1.pin_34, MCU1.pin_39, Part5.GND, Part6.GND, e-radionica_com1.GND
  N1: LED2.anode, R4.Pin_0
  N2: Part4.POS, Part5.POS
  N3: Part4.NEG, Part5.NEG
  N4: R4.Pin_1, MCU1.pin_7
  N5: MCU1.pin_1, MCU1.pin_17, Part6.VCC
  VCC: MCU1.pin_2, MCU1.pin_4, Part5.VCC, e-radionica_com1.VCC
  N6: MCU1.pin_3, e-radionica_com1.DO
  N7: MCU1.pin_5, Part6.DATA
  N8: MCU1.pin_40, Part5.DO

notes:
  (GPIO.BOARD)
  RED = 5V
  BLACK = GND
  GREEN = LDR GPIO 3
  YELLOW = DHT22 GPIO 5 BCM 3
  PINK = DHT22 3.3V POWER
  BLUE = LED GPIO 7
  WHITE = SOIL MOISTURE GPIO 40
  BREADBOARD ONLY NEEDED FOR LED
  These 2 wires dont have to be wired exactly this way they can be mixed
  USE BCM NUMBERING WHEN CODING DHT22 FOR WHICH PIN IS BEING USED FOR DATA

custom parts:
  FC-28 Soil Hygrometer Module - Probe: The FC-28 is a soil hygrometer module that uses the Texas Instruments LM393 comparator chip to provide an analog measurement of soil humidity.
  FC-28 Soil Hygrometer Module: The FC-28 is a soil hygrometer module that uses the Texas Instruments LM393 comparator chip to provide an analog measurement of soil humidity. The digital output is high when soil moisture is over a certain threshold, as determined by adjusting the potentiometer.
